# Fritzing sketch AOM_IoT_Bit (saved by Fritzing 0.9.3b)
breadboards: 1

parts:
  Mod1 = Arduino MKR Wifi 1010
  U1 = LittleBits w29 Perf [part_number=w29]
  R2 = Resistor [tolerance=±5% resistance=100 package=THT]
  S1 = Toggle Switch [package=THT]
  S2 = Toggle Switch [package=THT]
  LED1 = LED - 5mm [color="Red (633nm)" package="5 mm [THT]"]
  LED2 = LED - 5mm [color="Red (633nm)" package="5 mm [THT]"]
  R3 = Resistor [tolerance=±5% resistance=100 package=THT]
  R4 = Trimmer Potentiometer [maximum_resistance=10kΩ package=THT]

nets:
  GND: Mod1.GND, U1.gndOUT, U1.gndIN, U1.gnd3, S1.L1, LED1.cathode, LED2.cathode, R4.leg1
  N1: Mod1.A6, R4.wiper
  N2: Mod1.D0, U1.sigIN, U1.sigIN2
  N3: Mod1.D1, U1.sigOUT2
  N4: Mod1.~D2, S2.COM
  N5: Mod1.~D3, S1.COM
  N6: Mod1.D6, R2.Pin_1
  N7: Mod1.D7, R3.Pin_0
  N8: Mod1.VIN, U1.vccIN, U1.vccOUT, U1.vcc3, S1.L2, S2.L2, R4.leg2
  N9: R2.Pin_0, LED2.anode
  N10: LED1.anode, R3.Pin_1

custom parts:
  Arduino MKR Wifi 1010: Arduino MKR Wifi 1010, SAMD21 Cortex-M0+ 32bit Low Power ARM MCU,Flash Memory 256 KB, SRAM 32KB, 48mhz clock, Ublok Wifi interface.
  LittleBits w29 Perf: part for the littlebits w29 perf module
