# Fritzing sketch AOM_IoT_Bit_V3.0 (saved by Fritzing 0.9.9b)
breadboards: 1

parts:
  MKR_1010 = Arduino MKR Wifi 1010
  Post_Switch = Toggle Switch [package=THT]
  Get_Switch = Toggle Switch [package=THT]
  Post_LED = LED - 5mm [color="Red (633nm)" current=0.030 package="5 mm [THT]"]
  Get_LED = LED - 5mm [color="Red (633nm)" current=0.030 package="5 mm [THT]"]
  Post_LED_Res = Resistor [tolerance=±5% resistance=100 power=0.25 package=THT]
  Get_LED_Res = Resistor [tolerance=±5% resistance=100 power=0.25 package=THT]
  Conn_LED = LED - 5mm [color="Green (565nm)" current=0.030 package="5 mm [THT]"]
  Conn_LED_Res = Resistor [tolerance=±5% resistance=100 power=0.25 package=THT]
  SIGNAL_IN_R1 = Resistor [tolerance=±5% power=0.25 resistance=4.7k package=THT]
  S1 = Pushbutton [package="[THT]"]
  SIGNAL_IN = Header 3 [package=jst-3-smd]
  SIGNAL_OUT = Header 3 [package=jst-3-smd]
  SIGNAL_IN_R2 = Resistor [tolerance=±5% power=0.25 resistance=9.1k package=THT]
  C1 = Ceramic Capacitor [capacitance=100nF voltage=35V package="100 mil [THT, multilayer]"]
  Q3 = MOSFET-NCHANNEL [package=to-92]
  R1 = Resistor [tolerance=±5% power=0.25 resistance=10k package=THT]
  R2 = Resistor [tolerance=±5% power=0.25 resistance=10k package=THT]
  R_PU = Resistor [tolerance=±5% power=0.25 resistance=10k package=THT]

nets (from the schematic view):
  N1: MKR_1010.GND, Post_Switch.L1, Get_Switch.L1, Post_LED.cathode, Get_LED.cathode, Conn_LED.cathode, S1.Pin_1, S1.Pin_2, SIGNAL_IN.3, SIGNAL_OUT.3, SIGNAL_IN_R2.Pin_1, C1.1
  N2: MKR_1010.A1, Post_Switch.COM
  N3: MKR_1010.A2, Get_Switch.COM
  N4: MKR_1010.A3, Post_LED_Res.Pin_0
  N5: MKR_1010.A6, Get_LED_Res.Pin_0
  N6: MKR_1010.D0, Q3.S
  N7: MKR_1010.D1, SIGNAL_IN_R1.Pin_0, SIGNAL_IN_R2.Pin_0
  N8: MKR_1010.~D4, R_PU.Pin_0
  N9: MKR_1010.D6, Conn_LED_Res.Pin_0
  N10: MKR_1010.RESET, S1.Pin_3, S1.Pin_4
  N11: MKR_1010.+3V3, Post_Switch.L2, Get_Switch.L2, C1.0, R_PU.Pin_1
  N12: MKR_1010.VIN, SIGNAL_IN.1, SIGNAL_OUT.1, Q3.G, R1.Pin_0
  N13: MKR_1010.+5V, R2.Pin_0
  N14: Post_LED.anode, Post_LED_Res.Pin_1
  N15: Get_LED.anode, Get_LED_Res.Pin_1
  N16: Conn_LED.anode, Conn_LED_Res.Pin_1
  N17: SIGNAL_IN_R1.Pin_1, SIGNAL_IN.2
  N18: SIGNAL_OUT.2, Q3.D, R2.Pin_1

notes:
  Rev 2.0

custom parts:
  Arduino MKR Wifi 1010: Arduino MKR Wifi 1010, SAMD21 Cortex-M0+ 32bit Low Power ARM MCU,Flash Memory 256 KB, SRAM 32KB, 48mhz clock, Ublok Wifi interface.
