# Fritzing sketch AOM_IoT_Bit_V2.0 (saved by Fritzing 0.9.9b)
breadboards: 1

parts:
  Mod1 = Arduino MKR Wifi 1010
  S1 = Toggle Switch [package=THT]
  S2 = Toggle Switch [package=THT]
  LED1 = LED - 5mm [color="Red (633nm)" current=0.030 package="5 mm [THT]"]
  LED2 = LED - 5mm [color="Red (633nm)" current=0.030 package="5 mm [THT]"]
  R3 = Resistor [tolerance=±5% resistance=100 power=0.25 package=THT]
  R4 = Trimmer Potentiometer [maximum_resistance=10kΩ package=THT]
  U1 = LittleBits w29 Perf [part_number=w29]
  R5 = Resistor [tolerance=±5% resistance=100 power=0.25 package=THT]
  U2 = LittleBits w29 Perf [part_number=w29]
  LED3 = LED - 5mm [color="Blue (525nm)" current=0.030 package="5 mm [THT]"]
  R7 = Resistor [tolerance=±5% resistance=10k power=0.25 package=THT]
  LED4 = LED - 5mm [color="Red (633nm)" current=0.030 package="5 mm [THT]"]  # not connected
  LED5 = LED - 5mm [color="Blue (525nm)" current=0.030 package="5 mm [THT]"]  # not connected
  Mod2 = Arduino MKR Wifi 1010
  R8 = Resistor [tolerance=±5% resistance=100 power=0.25 package=THT]  # not connected
  R9 = Resistor [tolerance=±5% resistance=100 power=0.25 package=THT]  # not connected
  R10 = Resistor [tolerance=±5% resistance=10k power=0.25 package=THT]  # not connected
  LED6 = LED - 5mm [color="Red (633nm)" current=0.030 package="5 mm [THT]"]  # not connected
  S4 = Toggle Switch [package=THT]
  S5 = Toggle Switch [package=THT]
  R11 = Trimmer Potentiometer [maximum_resistance=10kΩ package=THT]
  S6 = Pushbutton [package="[THT]"]
  LED7 = LED - 3mm [color="Red (633nm)" current=0.030 package="3 mm [THT]"]  # not connected

nets:
  GND: Mod1.GND, S1.L1, LED1.cathode, LED2.cathode, R4.leg1, U1.gndOUT, U1.gndIN, U1.gnd3, LED3.cathode
  N1: Mod1.A1, R4.wiper
  N2: Mod1.A2, U1.sigOUT2
  N3: Mod1.A3, U1.sigIN, U1.sigIN2
  N4: Mod1.D0, R3.Pin_0
  N5: Mod1.D1, S1.COM
  N6: Mod1.~D2, R5.Pin_0
  N7: Mod1.~D3, S2.COM
  N8: Mod1.D6, R7.Pin_0
  N9: Mod1.VIN, S1.L2, S2.L2, R4.leg2, U1.vccIN, U1.vccOUT, U1.vcc3
  N10: LED1.anode, R3.Pin_1
  N11: LED2.anode, R5.Pin_1
  GND6: U2.gndIN, U2.gnd6, U2.gnd9, U2.gnd21, R11.leg1, S6.Pin_3, S6.Pin_4
  N12: U2.A4, Mod2.A1, R11.wiper
  N13: U2.B1, U2.B4, S6.Pin_1, S6.Pin_2
  N14: U2.B7, R11.leg2
  N15: U2.B13, S4.L1
  N16: U2.B15, S5.L1
  N17: U2.C13, S4.COM
  N18: U2.C15, S5.COM
  N19: U2.D13, S4.L2
  N20: U2.D15, S5.L2
  N21: LED3.anode, R7.Pin_1

notes:
  Debugging Model: Using a breadboard
  Compact Model
  In progress...

custom parts:
  Arduino MKR Wifi 1010: Arduino MKR Wifi 1010, SAMD21 Cortex-M0+ 32bit Low Power ARM MCU,Flash Memory 256 KB, SRAM 32KB, 48mhz clock, Ublok Wifi interface.
  LittleBits w29 Perf: part for the littlebits w29 perf module
