# Fritzing sketch AOM_IoT_Bit_V2.0_Mark_LogicConverter (saved by Fritzing 0.9.9b)
breadboards: 1

parts:
  MKR_1010 = Arduino MKR Wifi 1010
  Post_Switch = Toggle Switch [package=THT]
  Get_Switch = Toggle Switch [package=THT]
  Post_LED = LED - 5mm [color="Red (633nm)" current=0.030 package="5 mm [THT]"]
  Get_LED = LED - 5mm [color="Red (633nm)" current=0.030 package="5 mm [THT]"]
  Post_LED_Res = Resistor [tolerance=±5% resistance=100 power=0.25 package=THT]
  Get_LED_Res = Resistor [tolerance=±5% resistance=100 power=0.25 package=THT]
  Conn_LED = LED - 5mm [color="Blue (525nm)" current=0.030 package="5 mm [THT]"]
  Conn_LED_Res = Resistor [tolerance=±5% resistance=10k power=0.25 package=THT]
  S_IN_R2 = Resistor [tolerance=±5% resistance=3k power=0.25 package=THT]
  S_IN_R1 = Resistor [tolerance=±5% resistance=1.5k power=0.25 package=THT]
  LittleBits = LittleBits w29 Perf [part_number=w29]
  Part2 = I2C level shifter bidirectional

nets:
  GND: MKR_1010.GND, Post_Switch.L1, Get_Switch.L1, Post_LED.cathode, Get_LED.cathode, Conn_LED.cathode, S_IN_R2.Pin_1, LittleBits.gndIN, Part2.GND
  N1: MKR_1010.A1, Conn_LED_Res.Pin_0
  N2: MKR_1010.A2, Post_LED_Res.Pin_0
  N3: MKR_1010.A3, Post_Switch.COM
  N4: MKR_1010.A5, S_IN_R2.Pin_0, S_IN_R1.Pin_1
  N5: MKR_1010.A6, LittleBits.sigOUT, LittleBits.sigOUT1
  N6: MKR_1010.D0, Get_LED_Res.Pin_0
  N7: MKR_1010.D1, Get_Switch.COM
  N8: MKR_1010.+3V3, Post_Switch.L2, Get_Switch.L2, Part2.LV
  N9: MKR_1010.VIN, LittleBits.vccIN
  N10: MKR_1010.+5V, Part2.HV
  N11: Post_LED.anode, Post_LED_Res.Pin_1
  N12: Get_LED.anode, Get_LED_Res.Pin_1
  N13: Conn_LED.anode, Conn_LED_Res.Pin_1
  N14: S_IN_R1.Pin_0, LittleBits.sigIN, LittleBits.sigIN2
  N15: LittleBits.D4, LittleBits.D5, LittleBits.D6

notes:
  Rev 2.0

custom parts:
  Arduino MKR Wifi 1010: Arduino MKR Wifi 1010, SAMD21 Cortex-M0+ 32bit Low Power ARM MCU,Flash Memory 256 KB, SRAM 32KB, 48mhz clock, Ublok Wifi interface.
  LittleBits w29 Perf: part for the littlebits w29 perf module
